# Fritzing sketch sketch06 (saved by Fritzing 0.9.3b)
breadboards: 1

parts:
  부품1 = Arduino Uno (Rev3)
  S1 = Momentary Switch [package=ksa_sealed_tac_switch]
  R1 = Resistor [tolerance=±5% resistance=330 package=THT]
  LED1 = LED - 5mm [color="Green (570nm)" package="5 mm [THT]"]
  R2 = Resistor [tolerance=±5% resistance=110 package="1206 [SMD]"]

nets:
  N1: 부품1.D2, S1.1, S1.2, R1.Pin_0
  N2: 부품1.D4, R2.Pin_0
  N3: 부품1.5V, S1.3, S1.4
  N4: 부품1.GND, R1.Pin_1, LED1.cathode
  N5: LED1.anode, R2.Pin_1
